# Fritzing sketch chineserom_breakout (saved by Fritzing 0.9.2b)
circuit board: 4.18cm x 6.18cm
breadboards: 1

parts:
  IC1 = ChineseROM [chip_label=IC package=ChineseROM]
  J1 = female pin header, 22 pins [form="♀ (female)"]
  J2 = female pin header, 22 pins [form="♀ (female)"]
  J3 = female pin header, 6 pins [form="♀ (female)"]

nets:
  N1: IC1.1, J1.pin1
  N2: IC1.2, J1.pin2
  N3: IC1.3, J1.pin3
  N4: IC1.4, J1.pin4
  N5: IC1.5, J1.pin5
  N6: IC1.6, J1.pin6
  N7: IC1.7, J1.pin7
  N8: IC1.8, J1.pin8
  N9: IC1.9, J1.pin9
  N10: IC1.10, J1.pin10
  N11: IC1.11, J1.pin11
  N12: IC1.12, J1.pin12
  N13: IC1.13, J1.pin13
  N14: IC1.14, J1.pin14
  N15: IC1.15, J1.pin15
  N16: IC1.16, J1.pin16
  N17: IC1.17, J1.pin17
  N18: IC1.18, J1.pin18
  N19: IC1.19, J1.pin19
  N20: IC1.20, J1.pin20
  N21: IC1.21, J1.pin21
  N22: IC1.22, J1.pin22
  N23: IC1.23, J2.pin22
  N24: IC1.24, J2.pin21
  N25: IC1.25, J2.pin20
  N26: IC1.26, J2.pin19
  N27: IC1.27, J2.pin18
  N28: IC1.28, J2.pin17
  N29: IC1.29, J2.pin16
  N30: IC1.30, J2.pin15
  N31: IC1.31, J2.pin14
  N32: IC1.32, J2.pin13
  N33: IC1.33, J2.pin12
  N34: IC1.34, J2.pin11
  N35: IC1.35, J2.pin10
  N36: IC1.36, J2.pin9
  N37: IC1.37, J2.pin8
  N38: IC1.38, J2.pin7
  N39: IC1.39, J2.pin6
  N40: IC1.40, J2.pin5
  N41: IC1.41, J2.pin4
  N42: IC1.42, J2.pin3
  N43: IC1.43, J2.pin2
  N44: IC1.44, J2.pin1
  N45: IC1.45, J3.pin1
  N46: IC1.46, J3.pin2
  N47: IC1.47, J3.pin3
  N48: IC1.48, J3.pin4
  N49: IC1.49, J3.pin5
  N50: IC1.50, J3.pin6

notes:
  Beckie's ROM Tool
  SOP44/Chinese ROM
  Breakout Board
  A21
  A18
  A17
  A7
  A6
  A5
  A4
  A3
  A2
  A1
  A0
  #CE
  GND
  #OE
  Q0
  Q8
  Q1
  Q9
  Q2
  Q10
  Q3
  Q11
  A20
  A19
  A8
  A9
  A10
  Q12
  Q14
  A11
  A13
  Q15
  Q6
  Q13
  A16
  A14
  Q7
  A12
  VCC
  Q5
  Q4
  A15
