# Fritzing sketch romtool-shield (saved by Fritzing 0.9.2b)
circuit board: 10.1776cm x 5.36194cm
breadboards: 1

parts:
  J12 = female pin header, 8 pins [form="♀ (female)"]
  J13 = female pin header, 8 pins [form="♀ (female)"]  # not connected
  J18 = female pin header, 8 pins [form="♀ (female)"]
  J19 = double row female pin header, 36 pins [form="♀ (female)"]  # not connected
  J20 = female pin header, 8 pins [form="♀ (female)"]
  J21 = female pin header, 8 pins [form="♀ (female)"]  # not connected
  J22 = female pin header, 10 pins [form="♀ (female)"]
  J23 = double row female pin header, 20 pins [form="♀ (female)"]

nets:
  N1: J12.pin1, J23.pin6
  N2: J12.pin2, J23.pin5
  N3: J12.pin3, J23.pin4
  N4: J12.pin4, J23.pin3
  N5: J12.pin5, J23.pin12
  N6: J12.pin6, J23.pin13
  N7: J18.pin1, J23.pin14
  N8: J18.pin2, J23.pin15
  N9: J18.pin3, J23.pin16
  N10: J18.pin4, J23.pin17
  N11: J18.pin5, J23.pin18
  N12: J18.pin6, J23.pin19
  N13: J20.pin4, J23.pin10, J23.pin11
  N14: J22.pin5, J23.pin1
  N15: J22.pin6, J23.pin2
  N16: J22.pin7, J23.pin20
  N17: J22.pin8, J23.pin9
  N18: J22.pin9, J23.pin8
  N19: J22.pin10, J23.pin7

notes:
  SCL
  SDA
  AREF
  GND
  3.3V
  #CE
  Vin
  #WE
  #OE
  5V
  IOREF
  RX
  TX
  RESET
  A30
  A29
  A28
  A27
  A26
  A25
  A24
  A23
  A22
  A21
  A20
  A19
  A18
  A17
  A16
  A15
  A14
  A13
  A12
  A11
  A10
  A9
  A8
  A7
  A6
  A5
  A4
  A3
  A2
  A1
  A0
  GD
  15
  14
  13
  12
  11
  10
  Q9
  Q8
  Q7
  Q6
  Q5
  Q4
  3V
  Beckie's ROM Tool
