# Fritzing sketch romtool-shifter (saved by Fritzing 0.9.2b)
circuit board: 8.62cm x 6.92cm
breadboards: 1

parts:
  J24 = double row female pin header, 36 pins [form="♀ (female)"]
  J25 = double row female pin header, 20 pins [form="♀ (female)"]
  J26 = double row female pin header, 20 pins [form="♀ (female)"]
  J27 = double row female pin header, 36 pins [form="♀ (female)"]
  Part2 = SN74LVCH16T245 [part_number=SN74LVCH16T245 chip_label=SN74LVCH16T245 package=SSOP48]
  Part3 = SN74LVCH16T245 [part_number=SN74LVCH16T245 chip_label=SN74LVCH16T245 package=SSOP48]
  Part4 = SN74LVCH16T245 [part_number=SN74LVCH16T245 chip_label=SN74LVCH16T245 package=SSOP48]
  IC1 = SSOP16 [chip_label=IC package=SSOP]

nets:
  N1: J24.pin1, J24.pin36, J27.pin1, J27.pin36, Part2.VCCB, Part3.VCCB, Part4.VCCB, IC1.16
  N2: J24.pin2, Part4.2B8
  N3: J24.pin3, Part4.2B7
  N4: J24.pin4, Part4.2B6
  N5: J24.pin5, Part4.2B5
  N6: J24.pin6, Part4.2B4
  N7: J24.pin7, Part4.2B3
  N8: J24.pin8, Part4.2B2
  N9: J24.pin9, Part4.2B1
  N10: J24.pin10, Part2.1B8
  N11: J24.pin11, Part2.1B7
  N12: J24.pin12, Part2.1B6
  N13: J24.pin13, Part2.1B5
  N14: J24.pin14, Part2.1B4
  N15: J24.pin15, Part2.1B3
  N16: J24.pin16, Part2.1B2
  N17: J24.pin17, Part2.1B1
  GND: J24.pin18, J24.pin19, J27.pin18, J27.pin19, Part2.1DIR, Part2.GND, Part2.2DIR, Part2.2OE, Part2.1OE, Part3.GND, Part3.2OE, Part3.1OE, Part4.1DIR, Part4.GND, Part4.2DIR, Part4.2OE, Part4.1OE, IC1.4, IC1.5, IC1.6, IC1.7, IC1.8, IC1.9, IC1.10, IC1.11, IC1.12, IC1.13
  N18: J24.pin20, Part3.2B8
  N19: J24.pin21, Part3.2B7
  N20: J24.pin22, Part3.2B6
  N21: J24.pin23, Part3.2B5
  N22: J24.pin24, Part3.2B4
  N23: J24.pin25, Part3.2B3
  N24: J24.pin26, Part3.2B2
  N25: J24.pin27, Part3.2B1
  N26: J24.pin28, Part3.1B8
  N27: J24.pin29, Part3.1B7
  N28: J24.pin30, Part3.1B6
  N29: J24.pin31, Part3.1B5
  N30: J24.pin32, Part3.1B4
  N31: J24.pin33, Part3.1B3
  N32: J24.pin34, Part3.1B2
  N33: J24.pin35, Part3.1B1
  N34: J25.pin1, IC1.14
  N35: J25.pin2, Part2.2B8
  N36: J25.pin3, Part2.2B7
  N37: J25.pin4, Part2.2B6
  N38: J25.pin5, Part2.2B5
  N39: J25.pin6, Part2.2B4
  N40: J25.pin7, Part2.2B3
  N41: J25.pin8, Part2.2B2
  N42: J25.pin9, Part2.2B1
  N43: J25.pin10, J25.pin11, J26.pin10, J26.pin11, Part2.VCCA, Part3.VCCA, Part4.VCCA, IC1.1
  N44: J25.pin12, Part4.1B8
  N45: J25.pin13, Part4.1B7
  N46: J25.pin14, Part4.1B6
  N47: J25.pin15, Part4.1B5
  N48: J25.pin16, Part4.1B4
  N49: J25.pin17, Part4.1B3
  N50: J25.pin18, Part4.1B2
  N51: J25.pin19, Part4.1B1
  N52: J25.pin20, IC1.15
  N53: J26.pin1, Part3.1DIR, Part3.2DIR, IC1.2
  N54: J26.pin2, Part4.1A1
  N55: J26.pin3, Part4.1A2
  N56: J26.pin4, Part4.1A3
  N57: J26.pin5, Part4.1A4
  N58: J26.pin6, Part4.1A5
  N59: J26.pin7, Part4.1A6
  N60: J26.pin8, Part4.1A7
  N61: J26.pin9, Part4.1A8
  N62: J26.pin12, Part2.2A1
  N63: J26.pin13, Part2.2A2
  N64: J26.pin14, Part2.2A3
  N65: J26.pin15, Part2.2A4
  N66: J26.pin16, Part2.2A5
  N67: J26.pin17, Part2.2A6
  N68: J26.pin18, Part2.2A7
  N69: J26.pin19, Part2.2A8
  N70: J26.pin20, IC1.3
  N71: J27.pin2, Part3.1A1
  N72: J27.pin3, Part3.1A2
  N73: J27.pin4, Part3.1A3
  N74: J27.pin5, Part3.1A4
  N75: J27.pin6, Part3.1A5
  N76: J27.pin7, Part3.1A6
  N77: J27.pin8, Part3.1A7
  N78: J27.pin9, Part3.1A8
  N79: J27.pin10, Part3.2A1
  N80: J27.pin11, Part3.2A2
  N81: J27.pin12, Part3.2A3
  N82: J27.pin13, Part3.2A4
  N83: J27.pin14, Part3.2A5
  N84: J27.pin15, Part3.2A6
  N85: J27.pin16, Part3.2A7
  N86: J27.pin17, Part3.2A8
  N87: J27.pin20, Part2.1A1
  N88: J27.pin21, Part2.1A2
  N89: J27.pin22, Part2.1A3
  N90: J27.pin23, Part2.1A4
  N91: J27.pin24, Part2.1A5
  N92: J27.pin25, Part2.1A6
  N93: J27.pin26, Part2.1A7
  N94: J27.pin27, Part2.1A8
  N95: J27.pin28, Part4.2A1
  N96: J27.pin29, Part4.2A2
  N97: J27.pin30, Part4.2A3
  N98: J27.pin31, Part4.2A4
  N99: J27.pin32, Part4.2A5
  N100: J27.pin33, Part4.2A6
  N101: J27.pin34, Part4.2A7
  N102: J27.pin35, Part4.2A8

notes:
  3V
  A0
  A7
  A30
  A9
  A5
  Q4
  A19
  Q8
  A25
  A11
  GND
  #WE
  A26
  A15
  A1
  A6
  #OE
  A12
  A17
  A24
  A27
  A14
  A20
  Q5
  A22
  A23
  Q9
  A16
  #CE
  A21
  Q6
  A2
  A10
  A4
  A13
  A3
  A28
  A18
  A8
  A29
  Q7
  5V
  Q3
  Q2
  Q1
  Q0
  Q10
  Q11
  Q12
  Q13
  Q14
  Q15
  Beckie's ROM Tool - 5V to 3.3V Level Shifter
  3.3V
  SN74LVC2T45
  SN74LVCH16T245

custom parts:
  SN74LVCH16T245: The SN74LVCH16T245 device control pins (1DIR, 2DIR, 1OE, and 2OE) are supplied by VCCA. When OE is low and DIR is high, data transmission is from A to B. When OE is low and DIR is low, data transmission is from B to A. When OE is high, both output ports will be high-impedance.
